// Logisim project cs21_proj.circ as structural Verilog: 7 circuits, main circuit main
module main (
);

  wire cpu_alu_1_anyflow, cpu_alu_1_nbit, cpu_clk_out, cpu_ctrl_1_cfwrite, cpu_ctrl_1_memadd,
       cpu_ctrl_1_memwrite, cpu_ctrl_1_regwrite, cpu_regfile_1_cf, multiplexer_1_out;
  wire [1:0] cpu_ctrl_1_alusrca, cpu_ctrl_1_alusrcb, cpu_ctrl_1_cfsrc, cpu_ctrl_1_resultsrc;
  wire [2:0] cpu_ctrl_1_rd;
  wire [3:0] adder_1_out, bit_extender_1_out, cpu_alu_1_q, cpu_ctrl_1_aluop, cpu_regfile_1_acc,
       cpu_regfile_1_ra, cpu_regfile_1_rb, cpu_regfile_1_rc, cpu_regfile_1_rd, decode_type_1_instr_type,
       multiplexer_2_out, multiplexer_4_out, multiplexer_5_out, ram_1_dout;
  wire [7:0] multiplexer_3_out;
  wire [15:0] instr_mem_data, PC_q;

  Clock cpu_clk (.out(cpu_clk_out));
  Counter #(.max('hffff), .width(16)) PC (.count(1'b1), .Q(PC_q), .clk(cpu_clk_out));  // open: load, D, carry, up, clr
  ROM #(.addrWidth(16), .dataWidth(16)) instr_mem (.addr(PC_q), .data(instr_mem_data));
  // Probe on instr_mem_data
  // Probe on decode_type_1_instr_type
  decode_type decode_type_1 (.instr(instr_mem_data), .instr_type(decode_type_1_instr_type));
  cpu_ctrl cpu_ctrl_1 (
    .instr(instr_mem_data), .instr_type(decode_type_1_instr_type), .ALUOp(cpu_ctrl_1_aluop),
    .ALUSrcA(cpu_ctrl_1_alusrca), .ALUSrcB(cpu_ctrl_1_alusrcb), .ResultSrc(cpu_ctrl_1_resultsrc),
    .Rd(cpu_ctrl_1_rd), .MemAdd(cpu_ctrl_1_memadd), .MemWrite(cpu_ctrl_1_memwrite),
    .RegWrite(cpu_ctrl_1_regwrite), .CFWrite(cpu_ctrl_1_cfwrite), .CFSrc(cpu_ctrl_1_cfsrc));
  Multiplexer #(.select(2)) multiplexer_1 (
    .in0(1'b0), .in1(1'b1), .in2(cpu_alu_1_anyflow), .in3(cpu_alu_1_nbit), .out(multiplexer_1_out),
    .sel(cpu_ctrl_1_cfsrc));
  // Probe on cpu_ctrl_1_aluop
  // Probe on cpu_ctrl_1_alusrca
  // Probe on cpu_ctrl_1_alusrcb
  // Probe on cpu_ctrl_1_resultsrc
  // Probe on cpu_ctrl_1_rd
  // Probe on cpu_ctrl_1_memadd
  // Probe on multiplexer_5_out
  // Probe on cpu_ctrl_1_memwrite
  // Probe on cpu_ctrl_1_regwrite
  // Probe on cpu_ctrl_1_cfwrite
  // Probe on cpu_ctrl_1_cfsrc
  cpu_regfile cpu_regfile_1 (
    .WD3(multiplexer_5_out), .CFD(multiplexer_1_out), .WECF(cpu_ctrl_1_cfwrite), .Reset(1'b0),
    .CLK(cpu_clk_out), .WE3(cpu_ctrl_1_regwrite), .A1(cpu_ctrl_1_rd), .ACC(cpu_regfile_1_acc),
    .RA(cpu_regfile_1_ra), .RB(cpu_regfile_1_rb), .RC(cpu_regfile_1_rc), .RD(cpu_regfile_1_rd),
    .CF(cpu_regfile_1_cf));
  assign bit_extender_1_out = {{3{1'b0}}, cpu_regfile_1_cf};  // Bit_Extender bit_extender_1
  Adder #(.width(4)) adder_1 (.a(cpu_regfile_1_acc), .b(bit_extender_1_out), .out(adder_1_out));  // open: cin, cout
  Multiplexer #(.select(2), .width(4)) multiplexer_2 (
    .in0(cpu_regfile_1_acc), .in1(ram_1_dout), .in2(adder_1_out), .out(multiplexer_2_out),
    .sel(cpu_ctrl_1_alusrca));  // open: in3
  Multiplexer #(.width(8)) multiplexer_3 (
    .in0({cpu_regfile_1_rb, cpu_regfile_1_ra}), .in1({cpu_regfile_1_rd, cpu_regfile_1_rc}),
    .out(multiplexer_3_out), .sel(cpu_ctrl_1_memadd));
  // Probe on cpu_regfile_1_acc
  // Probe on cpu_regfile_1_ra
  // Probe on cpu_regfile_1_rb
  // Probe on cpu_regfile_1_rc
  // Probe on cpu_regfile_1_rd
  // Probe on cpu_regfile_1_cf
  Multiplexer #(.select(2), .width(4)) multiplexer_4 (
    .in0(ram_1_dout), .out(multiplexer_4_out), .sel(cpu_ctrl_1_alusrcb));  // open: in1, in2, in3
  // Probe on multiplexer_3_out
  // Probe on multiplexer_2_out
  cpu_alu cpu_alu_1 (
    .arg1(multiplexer_2_out), .arg2(multiplexer_4_out), .CF(cpu_regfile_1_cf), .ALUOp(cpu_ctrl_1_aluop),
    .anyflow(cpu_alu_1_anyflow), .q(cpu_alu_1_q), .NBit(cpu_alu_1_nbit));
  // Probe on cpu_alu_1_q
  RAM #(.asyncread("true"), .dataWidth(4)) ram_1 (
    .addr(multiplexer_3_out), .we(cpu_ctrl_1_memwrite), .oe(1'b1), .clk(cpu_clk_out),
    .din(cpu_regfile_1_acc), .dout(ram_1_dout));
  // Probe on ram_1_dout
  Multiplexer #(.select(2), .width(4)) multiplexer_5 (
    .in0(cpu_alu_1_q), .in1(ram_1_dout), .out(multiplexer_5_out), .sel(cpu_ctrl_1_resultsrc));  // open: in2, in3

  // Notes on the sheet:
  //   contents of instr_mem (hex, n*v repeats v):
  //   0 1 2 3 4 5 6 7 8 8 9 b 4*0 4*5 12*0 ffff 99*0 9*5 4 4
endmodule

module range_compare (
  input  [2:0] val,
  input  [2:0] lt,
  input  [2:0] gt,
  output q
);

  wire comparator_1_eq, comparator_1_lt, comparator_2_eq, comparator_2_gt, or_1_out, or_2_out;

  Comparator #(.width(3)) comparator_1 (.a(val), .b(lt), .eq(comparator_1_eq), .lt(comparator_1_lt));  // open: gt
  Comparator #(.width(3)) comparator_2 (.a(val), .b(gt), .gt(comparator_2_gt), .eq(comparator_2_eq));  // open: lt
  or or_1 (or_1_out, comparator_1_eq, comparator_1_lt);
  or or_2 (or_2_out, comparator_2_gt, comparator_2_eq);
  and and_1 (q, or_1_out, or_2_out);
endmodule

module decode_type (
  input  [15:0] instr,
  output [3:0] instr_type
);

  wire and_1_out, and_2_out, and_3_out, and_4_out, and_5_out, and_6_out, and_7_out, and_8_out, and_9_out,
       and_10_out, comparator_1_eq, comparator_2_eq, comparator_3_eq, comparator_4_eq, comparator_5_eq,
       comparator_6_eq, range_compare_1_q, range_compare_2_q, range_compare_3_q, range_compare_4_q,
       range_compare_5_q, range_compare_6_q, range_compare_7_q, range_compare_8_q;

  Comparator #(.width(5)) comparator_1 (.a(instr[7:3]), .b(5'b00111), .eq(comparator_1_eq));  // open: gt, lt
  Comparator #(.width(5)) comparator_2 (.a(instr[7:3]), .b(5'b00110), .eq(comparator_2_eq));  // open: gt, lt
  Comparator #(.width(5)) comparator_3 (.a(instr[7:3]), .b(5'b00101), .eq(comparator_3_eq));  // open: gt, lt
  Comparator #(.width(5)) comparator_4 (.a(instr[7:3]), .b(5'b00011), .eq(comparator_4_eq));  // open: gt, lt
  Comparator #(.width(5)) comparator_5 (.a(instr[7:3]), .b(5'b00001), .eq(comparator_5_eq));  // open: gt, lt
  Comparator #(.width(5)) comparator_6 (.a(instr[7:3]), .b({5{1'b0}}), .eq(comparator_6_eq));  // open: gt, lt
  range_compare range_compare_1 (.val(instr[2:0]), .lt(3'b011), .gt(3'b000), .q(range_compare_1_q));
  range_compare range_compare_2 (.val(instr[2:0]), .lt(3'b111), .gt(3'b100), .q(range_compare_2_q));
  range_compare range_compare_3 (.val(instr[2:0]), .lt(3'b111), .gt(3'b010), .q(range_compare_3_q));
  range_compare range_compare_4 (.val(instr[2:0]), .lt(3'b101), .gt(3'b010), .q(range_compare_4_q));
  range_compare range_compare_5 (.val(instr[2:0]), .lt(3'b111), .gt(3'b110), .q(range_compare_5_q));
  range_compare range_compare_6 (.val(instr[2:0]), .lt(3'b100), .gt(3'b010), .q(range_compare_6_q));
  range_compare range_compare_7 (.val(instr[2:0]), .lt(3'b001), .gt(3'b000), .q(range_compare_7_q));
  range_compare range_compare_8 (.val(instr[2:0]), .lt(3'b011), .gt(3'b010), .q(range_compare_8_q));
  and and_1 (and_1_out, range_compare_1_q, comparator_6_eq);
  and and_2 (and_2_out, range_compare_2_q, comparator_6_eq);
  and and_3 (and_3_out, comparator_5_eq, range_compare_1_q);
  and and_4 (and_4_out, comparator_5_eq, range_compare_2_q);
  and and_5 (and_5_out, comparator_4_eq, range_compare_3_q);
  and and_6 (and_6_out, range_compare_4_q, comparator_3_eq);
  and and_7 (and_7_out, range_compare_5_q, comparator_3_eq);
  and and_8 (and_8_out, range_compare_6_q, comparator_2_eq);
  and and_9 (and_9_out, range_compare_7_q, comparator_1_eq);
  and and_10 (and_10_out, range_compare_8_q, comparator_1_eq);
  Priority_Encoder #(.select(4)) priority_encoder_1 (
    .in0(and_1_out), .in1(and_2_out), .in2(and_3_out), .in3(and_4_out), .in4(and_5_out), .in5(and_6_out),
    .in6(and_7_out), .in7(and_8_out), .in8(and_9_out), .in9(and_10_out), .out(instr_type));  // open: in10, in11, in12, in13, in14, in15, gs, en_out, en_in
endmodule

module cpu_ctrl (
  input  [15:0] instr,
  input  [3:0] instr_type,
  output [3:0] ALUOp,
  output [1:0] ALUSrcA,
  output [1:0] ALUSrcB,
  output [1:0] ResultSrc,
  output [2:0] Rd,
  output MemAdd,
  output MemWrite,
  output RegWrite,
  output CFWrite,
  output [1:0] CFSrc
);

  wire multiplexer_2_out, multiplexer_3_out, not_1_out;
  wire [1:0] multiplexer_5_out;
  wire [3:0] multiplexer_1_out, multiplexer_4_out;
  wire [18:0] decode_joiner_1_opcodes, decode_joiner_2_opcodes, decode_joiner_3_opcodes;

  Multiplexer #(.width(4)) multiplexer_1 (.in0(4'b0010), .in1(4'b0011), .out(multiplexer_1_out), .sel(instr[1]));
  Multiplexer multiplexer_2 (.in0(1'b0), .in1(1'b1), .out(multiplexer_2_out), .sel(instr[1]));
  Multiplexer multiplexer_3 (.in0(1'b0), .in1(1'b1), .out(multiplexer_3_out), .sel(instr[0]));
  Multiplexer #(.select(2), .width(4)) multiplexer_4 (
    .in0(4'b0000), .in1(4'b0001), .in2(4'b0111), .in3(4'b1000), .out(multiplexer_4_out), .sel(instr[1:0]));
  Multiplexer #(.width(2)) multiplexer_5 (.in0(2'b10), .in1(2'b00), .out(multiplexer_5_out), .sel(instr[0]));
  not not_1 (not_1_out, multiplexer_3_out);
  decode_joiner decode_joiner_1 (
    .ALUOp(multiplexer_1_out), .ALUSrcA(multiplexer_5_out), .ALUSrcB(2'b00), .ResultSrc(2'b00), .Rd(3'b000),
    .MemAdd(1'b0), .MemWrite(1'b0), .RegWrite(1'b1), .CFWrite(1'b1), .CFSrc(2'b10),
    .opcodes(decode_joiner_1_opcodes));
  decode_joiner decode_joiner_2 (
    .ALUOp(4'b0000), .ALUSrcA(2'b00), .ALUSrcB(2'b00), .ResultSrc(2'b01), .Rd(3'b000),
    .MemAdd(multiplexer_2_out), .MemWrite(multiplexer_3_out), .RegWrite(not_1_out), .CFWrite(1'b0),
    .CFSrc(2'b00), .opcodes(decode_joiner_2_opcodes));
  decode_joiner decode_joiner_3 (
    .ALUOp(multiplexer_4_out), .ALUSrcA(2'b00), .ALUSrcB(2'b00), .ResultSrc(2'b00), .Rd(3'b000),
    .MemAdd(1'b0), .MemWrite(1'b0), .RegWrite(1'b1), .CFWrite(instr[1]), .CFSrc(2'b11),
    .opcodes(decode_joiner_3_opcodes));
  Multiplexer #(.select(4), .width(19)) multiplexer_6 (
    .in0(decode_joiner_3_opcodes), .in1(decode_joiner_2_opcodes), .in2(decode_joiner_1_opcodes),
    .out({CFSrc, CFWrite, RegWrite, MemWrite, MemAdd, Rd, ResultSrc, ALUSrcB, ALUSrcA, ALUOp}),
    .sel(instr_type));  // open: in3, in4, in5, in6, in7, in8, in9, in10, in11, in12, in13, in14, in15
  // Probe on instr_type

  // Notes on the sheet:
  //   ALUOp
  //   MemAdd
  //   MemWrite
  //   Type B (ACC to / from Mem)
  //   Type A (Rotation)
  //   ALU Operation
  //   RegWrite
  //   CFSrc
endmodule

module decode_joiner (
  input  [3:0] ALUOp,
  input  [1:0] ALUSrcA,
  input  [1:0] ALUSrcB,
  input  [1:0] ResultSrc,
  input  [2:0] Rd,
  input  MemAdd,
  input  MemWrite,
  input  RegWrite,
  input  CFWrite,
  input  [1:0] CFSrc,
  output [18:0] opcodes
);


  assign opcodes = {CFSrc, CFWrite, RegWrite, MemWrite, MemAdd, Rd, ResultSrc, ALUSrcB, ALUSrcA, ALUOp};
endmodule

module cpu_regfile (
  input  [3:0] WD3,
  input  CFD,
  input  WECF,
  input  Reset,
  input  CLK,
  input  WE3,
  input  [2:0] A1,
  output [3:0] ACC,
  output [3:0] RA,
  output [3:0] RB,
  output [3:0] RC,
  output [3:0] RD,
  output CF
);

  wire w0, w1, w2, w3, w4, w5, wr0, wr1, wr2, wr3, wr4, wr5;

  Register #(.width(4)) register_1 (.D(WD3), .en(w0), .clk(CLK), .Q(ACC), .clr(Reset));
  Register #(.width(4)) register_2 (.D(WD3), .en(w1), .clk(CLK), .Q(RA), .clr(Reset));
  Register #(.width(4)) register_3 (.D(WD3), .en(w2), .clk(CLK), .Q(RB), .clr(Reset));
  Register #(.width(4)) register_4 (.D(WD3), .en(w3), .clk(CLK), .Q(RC), .clr(Reset));
  Register #(.width(4)) register_5 (.D(WD3), .en(w4), .clk(CLK), .Q(RD), .clr(Reset));
  Register #(.width(1)) register_6 (.D(CFD), .en(WECF), .clk(CLK), .Q(CF), .clr(Reset));
  Decoder #(.select(3)) decoder_1 (
    .out0(wr0), .out1(wr1), .out2(wr2), .out3(wr3), .out4(wr4), .out5(wr5), .sel(A1));  // open: out6, out7, en
  and and_1 (w0, wr0, WE3);
  and and_2 (w1, wr1, WE3);
  and and_3 (w2, wr2, WE3);
  and and_4 (w3, wr3, WE3);
  and and_5 (w4, wr4, WE3);
  and and_6 (w5, wr5, WE3);

  // Other names for the same wires on the sheet: o0[3:0] = ACC
endmodule

module cpu_alu (
  input  [3:0] arg1,
  input  [3:0] arg2,
  input  CF,
  input  [3:0] ALUOp,
  output anyflow,
  output [3:0] q,
  output NBit
);

  wire adder_1_cout, subtractor_1_bout;
  wire [3:0] adder_1_out, and_1_out, or_1_out, subtractor_1_out, xor_1_out;

  assign and_1_out = arg1 & arg2;  // AND_Gate and_1, 4 bits wide
  assign or_1_out = arg1 | arg2;  // OR_Gate or_1, 4 bits wide
  assign xor_1_out = arg1 ^ arg2;  // XOR_Gate xor_1, 4 bits wide
  Adder #(.width(4)) adder_1 (.a(arg1), .b(arg2), .out(adder_1_out), .cout(adder_1_cout));  // open: cin
  Subtractor #(.width(4)) subtractor_1 (
    .a(arg1), .b(arg2), .out(subtractor_1_out), .bout(subtractor_1_bout));  // open: bin
  or or_2 (anyflow, adder_1_cout, subtractor_1_bout);
  Multiplexer #(.select(4)) multiplexer_1 (
    .in0(1'b0), .in1(1'b0), .in2(1'b0), .in3(1'b0), .in4(1'b0), .in5(1'b0), .in6(1'b0), .in7(arg1[0]),
    .in8(arg1[3]), .in9(1'b0), .in10(1'b0), .in11(1'b0), .in12(1'b0), .in13(1'b0), .in14(1'b0), .in15(1'b0),
    .out(NBit), .sel(ALUOp));
  Multiplexer #(.select(4), .width(4)) multiplexer_2 (
    .in0({arg1[0], arg1[3:1]}), .in1({arg1[2:0], arg1[3]}), .in2(adder_1_out), .in3(subtractor_1_out),
    .in4(and_1_out), .in5(or_1_out), .in6(xor_1_out), .in7({CF, arg1[3:1]}), .in8({arg1[2:0], CF}),
    .in9(4'b0000), .in10(4'b0000), .in11(4'b0000), .in12(4'b0000), .in13(4'b0000), .in14(4'b0000),
    .in15(4'b0000), .out(q), .sel(ALUOp));
endmodule
